// Logisim project CircuitoIntegrado.circ as structural Verilog: 1 circuit, main circuit main
module main (
  input  [2:0] CurrentState,
  input  [15:0] Instruction,
  input  [15:0] in_3,
  output [15:0] out_4,
  output [3:0] out_5
);

  wire clock_1_out, comparator_1_eq;
  wire [2:0] uc_1_p3;
  wire [3:0] R0_data_out, R1_data_out;
  wire [15:0] JumpDecoder_p4, main_1_out_3, multiplexer_1_out;

  Clock clock_1 (.out(clock_1_out));
  IR_main main_1 (.in_2(in_3), .in_1(clock_1_out), .out_3(main_1_out_3));
  // Uc uc_1: pin names not known; wires that end beside it: CurrentState, Instruction, uc_1_p3
  Multiplexer #(.width(16)) multiplexer_1 (
    .in0(main_1_out_3), .in1({16{1'b0}}), .out(multiplexer_1_out), .sel(1'b0));  // open: en
  Comparator #(.width(3)) comparator_1 (.a(uc_1_p3), .b(3'b111), .eq(comparator_1_eq));  // open: gt, lt
  Register R0 (.Data_In(multiplexer_1_out[11:8]), .Clock(clock_1_out), .Data_Out(R0_data_out));
  Register R1 (.Data_In(multiplexer_1_out[7:4]), .Clock(clock_1_out), .Data_Out(R1_data_out));
  // JumpDecoder JumpDecoder: pin names not known; wires that end beside it: 3'b111, {16{1'b0}}, in_3, JumpDecoder_p4
  ULA ula_1 (
    .Entry_A(R0_data_out), .Entry_B(R1_data_out), .OPCODE(multiplexer_1_out[15:12]), .Out(out_5));  // open: Carry__iN, Carry_Out
  Multiplexer #(.width(16)) multiplexer_2 (
    .in0({16{1'b0}}), .in1(JumpDecoder_p4), .out(out_4), .sel(comparator_1_eq));  // open: en

  // Notes on the sheet:
  //   - primeiros testes...
  //   começando a integrar as partes
  //   PC
  //   PC
endmodule
